# Fritzing sketch gpizero-mqtt-robot (saved by Fritzing 0.9.3b)

parts:
  Raspberry_Pi_Zero1 = Raspberry Pi Zero
  M1 = DC Motor
  M2 = DC Motor
  U1 = L9110 H-bridge module [part_number="L9110 H-bridge"]

nets:
  N1: Raspberry_Pi_Zero1.GIPO4, U1.B-IA
  N2: Raspberry_Pi_Zero1.GIPO17, U1.A-IB
  N3: Raspberry_Pi_Zero1.GIPO18, U1.A-IA
  N4: Raspberry_Pi_Zero1.GIPO14, U1.B-IB
  GND: Raspberry_Pi_Zero1.GND, U1.GND
  5V: Raspberry_Pi_Zero1.5V, U1.VCC
  N5: M1.pin_1, U1.MOTOR_B-B
  N6: M1.pin_2, U1.MOTOR_B-A
  N7: M2.pin_1, U1.MOTOR_A-B
  N8: M2.pin_2, U1.MOTOR_A-A
